// Logisim project Wolf Sheep Cabbage Problem.circ as structural Verilog: 12 circuits, main circuit main
module main (
);

  wire and_1_out, C_out, clock_1_out_3, clock_1_out_4, clock_1_out_5, clock_1_out_6, clock_1_out_7,
       clock_1_out_8, clock_1_out_9, clock_1_out_10, clock_1_out_11, F_out, main_circuit_1_cabbage_2,
       main_circuit_1_farmer_2, main_circuit_1_sheep_2, main_circuit_1_wolf_2, n1st_7seg_1_c, n1st_7seg_1_d,
       n1st_7seg_1_e, n1st_7seg_1_f, n1st_7seg_1_g, n1st_7seg_1_out_8, n1st_7seg_1_out_9, n2nd_7seg_1_c,
       n2nd_7seg_1_d, n2nd_7seg_1_e, n2nd_7seg_1_f, n2nd_7seg_1_g, n2nd_7seg_1_out_8, n2nd_7seg_1_out_9,
       n3rd_7seg_1_c, n3rd_7seg_1_d, n3rd_7seg_1_e, n3rd_7seg_1_f, n3rd_7seg_1_g, n3rd_7seg_1_out_8,
       n3rd_7seg_1_out_9, n4th_7seg_1_c, n4th_7seg_1_d, n4th_7seg_1_e, n4th_7seg_1_f, n4th_7seg_1_g,
       n4th_7seg_1_out_8, n4th_7seg_1_out_9, n7_segment_1_a, n7_segment_1_b, n7_segment_1_c, n7_segment_1_d,
       n7_segment_1_e, n7_segment_1_f, n7_segment_1_g, n7_segment_2_a, n7_segment_2_b, n7_segment_2_c,
       n7_segment_2_d, n7_segment_2_e, n7_segment_2_f, n7_segment_2_g, not_1_out, not_2_out, not_3_out,
       not_4_out, R_out, S_out, W_out;

  LED led_1 (.in(not_4_out));
  LED led_2 (.in(not_3_out));
  LED led_3 (.in(not_2_out));
  LED led_4 (.in(not_1_out));
  Button F (.out(F_out));
  Button R (.out(R_out));
  _7_segment u_7_segment_1 (
    .W(clock_1_out_7), .X(clock_1_out_6), .Y(clock_1_out_5), .Z(clock_1_out_4), .a(n7_segment_1_a),
    .b(n7_segment_1_b), .c(n7_segment_1_c), .d(n7_segment_1_d), .e(n7_segment_1_e), .f(n7_segment_1_f),
    .g(n7_segment_1_g));
  _7_Segment_Display u_7_segment_display_1 (
    .g(n7_segment_2_g), .f(n7_segment_2_f), .a(n7_segment_2_a), .b(n7_segment_2_b), .e(n7_segment_2_e),
    .d(n7_segment_2_d), .c(n7_segment_2_c));  // open: dp
  _7_Segment_Display u_7_segment_display_2 (
    .g(n7_segment_1_g), .f(n7_segment_1_f), .a(n7_segment_1_a), .b(n7_segment_1_b), .e(n7_segment_1_e),
    .d(n7_segment_1_d), .c(n7_segment_1_c));  // open: dp
  LED led_5 (.in(and_1_out));
  LED led_6 (.in(and_1_out));
  LED led_7 (.in(and_1_out));
  LED led_8 (.in(and_1_out));
  not not_1 (not_1_out, main_circuit_1_cabbage_2);
  not not_2 (not_2_out, main_circuit_1_sheep_2);
  not not_3 (not_3_out, main_circuit_1_wolf_2);
  not not_4 (not_4_out, main_circuit_1_farmer_2);
  Button W (.out(W_out));
  Button S (.out(S_out));
  _7_segment u_7_segment_2 (
    .W(clock_1_out_11), .X(clock_1_out_10), .Y(clock_1_out_9), .Z(clock_1_out_8), .a(n7_segment_2_a),
    .b(n7_segment_2_b), .c(n7_segment_2_c), .d(n7_segment_2_d), .e(n7_segment_2_e), .f(n7_segment_2_f),
    .g(n7_segment_2_g));
  LED led_9 (.in(and_1_out));
  LED led_10 (.in(and_1_out));
  LED led_11 (.in(main_circuit_1_farmer_2));
  LED led_12 (.in(main_circuit_1_wolf_2));
  LED led_13 (.in(main_circuit_1_sheep_2));
  LED led_14 (.in(main_circuit_1_cabbage_2));
  Button C (.out(C_out));
  Clock clock_1 (
    .out_4(clock_1_out_4), .out_5(clock_1_out_5), .out_6(clock_1_out_6), .out_7(clock_1_out_7),
    .out_8(clock_1_out_8), .out_9(clock_1_out_9), .out_10(clock_1_out_10), .out_11(clock_1_out_11),
    .Reset_Timer(R_out), .in_2(and_1_out), .out_3(clock_1_out_3));
  and and_1 (and_1_out, main_circuit_1_farmer_2, main_circuit_1_wolf_2, main_circuit_1_sheep_2, main_circuit_1_cabbage_2);
  main_circuit main_circuit_1 (
    .Cabbage(C_out), .Sheep(S_out), .Wolf(W_out), .Farmer(F_out), .Reset_Game(R_out),
    .Farmer_2(main_circuit_1_farmer_2), .Wolf_2(main_circuit_1_wolf_2), .Sheep_2(main_circuit_1_sheep_2),
    .Cabbage_2(main_circuit_1_cabbage_2));
  _1st_7seg u_1st_7seg_1 (
    .X(and_1_out), .Y(clock_1_out_3), .g(n1st_7seg_1_g), .f(n1st_7seg_1_f), .e(n1st_7seg_1_e),
    .d(n1st_7seg_1_d), .c(n1st_7seg_1_c), .out_8(n1st_7seg_1_out_8), .out_9(n1st_7seg_1_out_9));
  _7_Segment_Display u_7_segment_display_3 (
    .g(n1st_7seg_1_g), .f(n1st_7seg_1_f), .a(n1st_7seg_1_out_9), .b(n1st_7seg_1_out_8), .e(n1st_7seg_1_e),
    .d(n1st_7seg_1_d), .c(n1st_7seg_1_c));  // open: dp
  _2nd_7seg u_2nd_7seg_1 (
    .X(and_1_out), .Y(clock_1_out_3), .g(n2nd_7seg_1_g), .f(n2nd_7seg_1_f), .e(n2nd_7seg_1_e),
    .d(n2nd_7seg_1_d), .c(n2nd_7seg_1_c), .out_8(n2nd_7seg_1_out_8), .out_9(n2nd_7seg_1_out_9));
  _7_Segment_Display u_7_segment_display_4 (
    .g(n2nd_7seg_1_g), .f(n2nd_7seg_1_f), .a(n2nd_7seg_1_out_9), .b(n2nd_7seg_1_out_8), .e(n2nd_7seg_1_e),
    .d(n2nd_7seg_1_d), .c(n2nd_7seg_1_c));  // open: dp
  _7_Segment_Display u_7_segment_display_5 (
    .g(n3rd_7seg_1_g), .f(n3rd_7seg_1_f), .a(n3rd_7seg_1_out_9), .b(n3rd_7seg_1_out_8), .e(n3rd_7seg_1_e),
    .d(n3rd_7seg_1_d), .c(n3rd_7seg_1_c));  // open: dp
  _3rd_7seg u_3rd_7seg_1 (
    .X(and_1_out), .Y(clock_1_out_3), .g(n3rd_7seg_1_g), .f(n3rd_7seg_1_f), .e(n3rd_7seg_1_e),
    .d(n3rd_7seg_1_d), .c(n3rd_7seg_1_c), .out_8(n3rd_7seg_1_out_8), .out_9(n3rd_7seg_1_out_9));
  _7_Segment_Display u_7_segment_display_6 (
    .g(n4th_7seg_1_g), .f(n4th_7seg_1_f), .a(n4th_7seg_1_out_9), .b(n4th_7seg_1_out_8), .e(n4th_7seg_1_e),
    .d(n4th_7seg_1_d), .c(n4th_7seg_1_c));  // open: dp
  _4th_7seg u_4th_7seg_1 (
    .X(and_1_out), .Y(clock_1_out_3), .g(n4th_7seg_1_g), .f(n4th_7seg_1_f), .e(n4th_7seg_1_e),
    .d(n4th_7seg_1_d), .c(n4th_7seg_1_c), .out_8(n4th_7seg_1_out_8), .out_9(n4th_7seg_1_out_9));

  // Notes on the sheet:
  //   Reset Game
  //   Farmer
  //   Wolf
  //   Sheep
  //   Cabbage
endmodule

module Farmer_Moves_Alone (
  input  F,
  input  W,
  input  S,
  input  C,
  output out_5
);

  wire and_1_out, and_2_out, not_1_out, not_2_out, not_3_out;

  not not_1 (not_1_out, S);
  and and_1 (and_1_out, W, not_1_out, C);
  not not_2 (not_2_out, W);
  and and_2 (and_2_out, not_2_out, S, not_3_out);
  not not_3 (not_3_out, C);
  or or_1 (out_5, and_1_out, and_2_out);
endmodule

module Farmer_Moves_Wolf (
  input  F,
  input  W,
  input  S,
  input  C,
  output out_5
);

  wire and_1_out, and_2_out, and_3_out, and_4_out, not_1_out, not_2_out, not_3_out, not_4_out, not_5_out,
       not_6_out, not_7_out, not_8_out;

  not not_1 (not_1_out, F);
  not not_2 (not_2_out, W);
  not not_3 (not_3_out, S);
  not not_4 (not_4_out, F);
  not not_5 (not_5_out, W);
  not not_6 (not_6_out, C);
  not not_7 (not_7_out, S);
  not not_8 (not_8_out, C);
  and and_1 (and_1_out, not_1_out, not_2_out, not_3_out, C);
  and and_2 (and_2_out, not_4_out, not_5_out, S, not_6_out);
  and and_3 (and_3_out, F, W, not_7_out, C);
  and and_4 (and_4_out, F, W, S, not_8_out);
  or or_1 (out_5, and_1_out, and_2_out, and_3_out, and_4_out);
endmodule

module Farmer_Moves_Sheep (
  input  F,
  input  W,
  input  S,
  input  C,
  output out_5
);

  xnor xnor_1 (out_5, S, F);
endmodule

module Farmer_Moves_Cabbage (
  input  F,
  input  W,
  input  S,
  input  C,
  output out_5
);

  wire and_1_out, and_2_out, and_3_out, and_4_out, not_1_out, not_2_out, not_3_out, not_4_out, not_5_out,
       not_6_out, not_7_out, not_8_out;

  not not_1 (not_1_out, F);
  not not_2 (not_2_out, W);
  not not_3 (not_3_out, C);
  not not_4 (not_4_out, F);
  not not_5 (not_5_out, S);
  not not_6 (not_6_out, C);
  not not_7 (not_7_out, W);
  not not_8 (not_8_out, S);
  and and_1 (and_1_out, not_1_out, not_2_out, S, not_3_out);
  and and_2 (and_2_out, not_4_out, W, not_5_out, not_6_out);
  and and_3 (and_3_out, F, not_7_out, S, C);
  and and_4 (and_4_out, F, W, not_8_out, C);
  or or_1 (out_5, and_1_out, and_2_out, and_3_out, and_4_out);
endmodule

module _7_segment (
  input  W,
  input  X,
  input  Y,
  input  Z,
  output a,
  output b,
  output c,
  output d,
  output e,
  output f,
  output g
);

  wire and_1_out, and_2_out, and_3_out, and_4_out, and_5_out, and_6_out, and_7_out, and_8_out, not_1_out,
       not_2_out, not_3_out, or_1_out, or_2_out, or_3_out, xnor_1_out, xnor_2_out;

  not not_1 (not_1_out, Z);
  not not_2 (not_2_out, X);
  not not_3 (not_3_out, Y);
  or or_1 (or_1_out, Y, not_1_out);
  or or_2 (or_2_out, not_2_out, Y);
  and and_1 (and_1_out, not_3_out, not_1_out);
  and and_2 (and_2_out, X, not_1_out);
  and and_3 (and_3_out, X, not_3_out);
  and and_4 (and_4_out, Y, or_3_out);
  or or_3 (or_3_out, not_2_out, not_1_out);
  and and_5 (and_5_out, X, not_3_out);
  xnor xnor_1 (xnor_1_out, Z, X);
  xnor xnor_2 (xnor_2_out, Y, Z);
  and and_6 (and_6_out, or_1_out, not_2_out);
  and and_7 (and_7_out, Y, not_1_out);
  and and_8 (and_8_out, X, not_3_out, Z);
  or or_4 (a, W, Y, xnor_1_out);
  or or_5 (b, xnor_2_out, not_2_out);
  or or_6 (c, X, not_3_out, Z);
  or or_7 (d, W, and_6_out, and_7_out, and_8_out);
  and and_9 (e, not_1_out, or_2_out);
  or or_8 (f, and_1_out, and_2_out, and_3_out, W);
  or or_9 (g, W, and_4_out, and_5_out);
endmodule

module main_circuit (
  input  Cabbage,
  input  Sheep,
  input  Wolf,
  input  Farmer,
  input  Reset_Game,
  output Farmer_2,
  output Wolf_2,
  output Sheep_2,
  output Cabbage_2
);

  wire and_1_out, and_2_out, and_3_out, and_4_out, clock_1_out, farmer_moves_alone_1_out_5,
       farmer_moves_cabbage_1_out_5, farmer_moves_sheep_1_out_5, farmer_moves_wolf_1_out_5,
       multiplexer_1_out, multiplexer_2_out, multiplexer_3_out, multiplexer_4_out, not_1_out, not_2_out,
       not_3_out, not_4_out, or_1_out;

  Farmer_Moves_Alone farmer_moves_alone_1 (
    .out_5(farmer_moves_alone_1_out_5), .F(Farmer_2), .W(Wolf_2), .S(Sheep_2), .C(Cabbage_2));
  Farmer_Moves_Wolf farmer_moves_wolf_1 (
    .out_5(farmer_moves_wolf_1_out_5), .F(Farmer_2), .W(Wolf_2), .S(Sheep_2), .C(Cabbage_2));
  or or_1 (or_1_out, and_1_out, and_2_out, and_3_out, and_4_out);
  Farmer_Moves_Sheep farmer_moves_sheep_1 (
    .out_5(farmer_moves_sheep_1_out_5), .F(Farmer_2), .W(Wolf_2), .S(Sheep_2), .C(Cabbage_2));
  and and_1 (and_1_out, Cabbage, farmer_moves_cabbage_1_out_5);
  and and_2 (and_2_out, Sheep, farmer_moves_sheep_1_out_5);
  and and_3 (and_3_out, Wolf, farmer_moves_wolf_1_out_5);
  and and_4 (and_4_out, Farmer, farmer_moves_alone_1_out_5);
  Farmer_Moves_Cabbage farmer_moves_cabbage_1 (
    .out_5(farmer_moves_cabbage_1_out_5), .F(Farmer_2), .W(Wolf_2), .S(Sheep_2), .C(Cabbage_2));
  Register #(.width(1)) register_1 (
    .D(multiplexer_1_out), .en(or_1_out), .Q(Farmer_2), .clk(clock_1_out), .clr(Reset_Game));
  Multiplexer #(.enable("false")) multiplexer_1 (
    .in0(Farmer_2), .in1(not_1_out), .out(multiplexer_1_out), .sel(or_1_out));
  not not_1 (not_1_out, Farmer_2);
  Register #(.width(1)) register_2 (
    .D(multiplexer_2_out), .Q(Wolf_2), .clk(clock_1_out), .clr(Reset_Game));  // open: en
  Multiplexer #(.enable("false")) multiplexer_2 (
    .in0(Wolf_2), .in1(not_2_out), .out(multiplexer_2_out), .sel(and_3_out));
  not not_2 (not_2_out, Wolf_2);
  Register #(.width(1)) register_3 (
    .D(multiplexer_3_out), .Q(Sheep_2), .clk(clock_1_out), .clr(Reset_Game));  // open: en
  Multiplexer #(.enable("false")) multiplexer_3 (
    .in0(Sheep_2), .in1(not_3_out), .out(multiplexer_3_out), .sel(and_2_out));
  not not_3 (not_3_out, Sheep_2);
  Register #(.width(1)) register_4 (
    .D(multiplexer_4_out), .Q(Cabbage_2), .clk(clock_1_out), .clr(Reset_Game));  // open: en
  Clock_part #(.lowDuration(10)) clock_1 (.out(clock_1_out));
  Multiplexer #(.enable("false")) multiplexer_4 (
    .in0(Cabbage_2), .in1(not_4_out), .out(multiplexer_4_out), .sel(and_1_out));
  not not_4 (not_4_out, Cabbage_2);

  // Notes on the sheet:
  //   Check whether the move is legal
  //   Memory for each State
  //   Bit Inverter
  //   Check whether they update
endmodule

module Clock (
  input  Reset_Timer,
  input  in_2,
  output out_3,
  output out_4,
  output out_5,
  output out_6,
  output out_7,
  output out_8,
  output out_9,
  output out_10,
  output out_11
);

  wire and_1_out, and_2_out, and_3_out, and_4_out, clock_1_out, multiplexer_1_out, not_1_out, not_2_out,
       not_3_out, or_1_out;
  wire [3:0] counter_3_q;
  wire [5:0] counter_4_q, multiplexer_2_out;

  and and_1 (and_1_out, out_9, out_11);
  and and_2 (and_2_out, out_8, out_11, out_4, out_7);
  Multiplexer #(.enable("false")) multiplexer_1 (
    .in0(and_1_out), .in1(1'b1), .out(multiplexer_1_out), .sel(Reset_Timer));
  Counter #(.width(4), .max('hf)) counter_1 (
    .Q({out_7, out_6, out_5, out_4}), .clk(and_4_out), .clr(Reset_Timer));  // open: load, D, count, carry
  Counter #(.width(4), .max('hf)) counter_2 (
    .Q({out_11, out_10, out_9, out_8}), .clk(and_3_out), .clr(multiplexer_1_out));  // open: load, D, count, carry
  and and_3 (and_3_out, not_1_out, multiplexer_2_out[5], multiplexer_2_out[4], multiplexer_2_out[3], multiplexer_2_out[1], multiplexer_2_out[0]);
  not not_1 (not_1_out, multiplexer_2_out[2]);
  Counter #(.width(4), .max('hf)) counter_3 (
    .Q(counter_3_q), .clk(and_3_out), .clr(and_4_out));  // open: load, D, count, carry
  and and_4 (and_4_out, counter_3_q[3], not_2_out, counter_3_q[1], not_3_out);
  Multiplexer #(.width(6), .enable("false")) multiplexer_2 (
    .in0(counter_4_q), .in1({6{1'b0}}), .out(multiplexer_2_out), .sel(or_1_out));
  not not_2 (not_2_out, counter_3_q[2]);
  not not_3 (not_3_out, counter_3_q[0]);
  or or_1 (or_1_out, in_2, out_3);
  Counter #(.width(6), .max('h3f)) counter_4 (
    .Q(counter_4_q), .clk(clock_1_out), .clr(multiplexer_1_out));  // open: load, D, count, carry
  Clock_part #(.lowDuration(10)) clock_1 (.out(clock_1_out));
  Register #(.width(1)) register_1 (.D(and_2_out), .Q(out_3), .clk(clock_1_out));  // open: en, clr

  // Notes on the sheet:
  //   Second Digit on the Clock
  //   7 Segment Input
  //   First Digit on the Clock
  //   Stop Timer
  //   Fail when Time reaches 99
endmodule

module _1st_7seg (
  input  X,
  input  Y,
  output g,
  output f,
  output e,
  output d,
  output c,
  output out_8,
  output out_9
);

  wire not_1_out, not_2_out;

  xor xor_1 (e, X, Y);
  not not_1 (not_1_out, X);
  and and_1 (f, not_1_out, Y);
  not not_2 (not_2_out, Y);
  and and_2 (c, not_2_out, X);

  assign d = c;
  assign g = e;
  assign out_8 = c;
  assign out_9 = f;

  // Notes on the sheet:
  //   7 Segment Display for Blank, f, d
  //   b
  //   a
endmodule

module _2nd_7seg (
  input  X,
  input  Y,
  output g,
  output f,
  output e,
  output d,
  output c,
  output out_8,
  output out_9
);

  wire not_1_out, not_2_out;

  xor xor_1 (c, X, Y);
  not not_1 (not_1_out, X);
  and and_1 (g, not_1_out, Y);
  not not_2 (not_2_out, Y);
  and and_2 (d, not_2_out, X);

  assign e = c;
  assign f = c;
  assign out_8 = c;
  assign out_9 = c;

  // Notes on the sheet:
  //   7 Segment Display for Blank, a, o
  //   b
  //   a
endmodule

module _3rd_7seg (
  input  X,
  input  Y,
  output g,
  output f,
  output e,
  output d,
  output c,
  output out_8,
  output out_9
);

  wire not_1_out, not_2_out;

  xor xor_1 (c, X, Y);
  not not_1 (not_1_out, X);
  // AND_Gate and_1 has open pins: in0=not_1_out, in1=Y, out=open
  not not_2 (not_2_out, Y);
  and and_2 (e, not_2_out, X);

  assign d = 1'b0;
  assign f = e;
  assign g = 1'b0;
  assign out_8 = c;
  assign out_9 = e;

  // Notes on the sheet:
  //   7 Segment Display for Blank, i, n
  //   b
  //   a
endmodule

module _4th_7seg (
  input  X,
  input  Y,
  output g,
  output f,
  output e,
  output d,
  output c,
  output out_8,
  output out_9
);

  wire not_1_out, not_2_out;

  xor xor_1 (d, X, Y);
  not not_1 (not_1_out, X);
  // AND_Gate and_1 has open pins: in0=not_1_out, in1=Y, out=open
  not not_2 (not_2_out, Y);
  and and_2 (g, not_2_out, X);

  assign c = 1'b0;
  assign e = d;
  assign f = d;
  assign out_8 = 1'b0;
  assign out_9 = g;

  // Notes on the sheet:
  //   7 Segment Display for Blank, l, e
  //   b
  //   a
endmodule
